// Logisim project processador.circ as structural Verilog: 6 circuits, main circuit ProgramCounter
module ProgramCounter (
  input  [23:0] data,
  input  W_PC,
  input  Clk,
  input  Reset,
  output [23:0] Pc_mais_1,
  output [23:0] Pc_out
);

  Register #(.width(24)) register_1 (.D(data), .en(W_PC), .clk(Clk), .Q(Pc_out), .clr(Reset));
  Adder #(.width(24)) adder_1 (.a(Pc_out), .b(24'h1), .out(Pc_mais_1));  // open: cin, cout
endmodule

module Main (
  input  MANUAL_RESET_RG,
  input  MANUAL_RESET
);

  wire B, branches_1_b_out, clk, IMM_ULA, or_1_out, or_2_out, RESET, W_MEM, W_PC, W_RG;
  wire [1:0] B_IN, D_RG, multiplexer_2_out, PC_M;
  wire [2:0] OP_ULA;
  wire [3:0] rom_1_data, rom_1_data_2, rom_1_data_3, rom_1_data_4;
  wire [7:0] rom_1_data_5;
  wire [23:0] bit_extender_1_out, bit_extender_5_out, multiplexer_1_out, pc_imm, Pc_mais_1,
       programcounter_1_pc_out, rs1_imm;
  wire [31:0] bit_extender_4_out, Imm, mem_out, multiplexer_3_out, multiplexer_4_out, rs1_out, rs2_out,
       Ula_result;

  Multiplexer #(.select(2), .width(24)) multiplexer_1 (
    .in0(Pc_mais_1), .in1(pc_imm), .in2(rs1_imm), .out(multiplexer_1_out), .sel(multiplexer_2_out));  // open: in3
  Multiplexer #(.width(2)) multiplexer_2 (.in0(PC_M), .in1(2'b01), .out(multiplexer_2_out), .sel(branches_1_b_out));
  or or_1 (or_1_out, MANUAL_RESET, RESET);
  branches branches_1 (.rs1(rs1_out), .rs2(rs2_out), .B_in(B_IN), .B(B), .B_out(branches_1_b_out));
  Clock clock_1 (.out(clk));
  ProgramCounter programcounter_1 (
    .data(multiplexer_1_out), .W_PC(W_PC), .Clk(clk), .Reset(or_1_out), .Pc_mais_1(Pc_mais_1),
    .Pc_out(programcounter_1_pc_out));
  Bit_Extender #(.in_width(32), .out_width(24)) bit_extender_1 (.in(Imm), .out(bit_extender_1_out));
  Bit_Extender #(.in_width(32), .out_width(24)) bit_extender_2 (.in(Ula_result), .out(rs1_imm));
  Adder #(.width(24)) adder_1 (.a(programcounter_1_pc_out), .b(bit_extender_1_out), .out(pc_imm));  // open: cin, cout
  ROM #(.addrWidth(24), .dataWidth(24)) rom_1 (
    .addr(programcounter_1_pc_out),
    .data({rom_1_data_5, rom_1_data_3, rom_1_data_4, rom_1_data_2, rom_1_data}));
  or or_2 (or_2_out, MANUAL_RESET_RG, RESET);
  assign Imm = {{24{rom_1_data_5[7]}}, rom_1_data_5};  // Bit_Extender bit_extender_3
  unit_control unit_control_1 (
    .OpCode(rom_1_data_3), .IMM_ULA(IMM_ULA), .W_RG(W_RG), .W_MEM(W_MEM), .PC_M(PC_M), .B(B), .D_RG(D_RG),
    .B_IN(B_IN), .OP_ULA(OP_ULA), .W_PC(W_PC), .RESET(RESET));
  banco_reg banco_reg_1 (
    .RS1_in(rom_1_data_2), .RS2_in(rom_1_data_4), .CLK(clk), .D(multiplexer_3_out), .Reset(or_2_out),
    .WE(W_RG), .rd(rom_1_data), .RS1_out(rs1_out), .RS2_out(rs2_out));
  Multiplexer #(.select(2), .width(32)) multiplexer_3 (
    .in0(Ula_result), .in1(mem_out), .in2(bit_extender_4_out), .out(multiplexer_3_out), .sel(D_RG));  // open: in3
  assign bit_extender_4_out = {{8{Pc_mais_1[23]}}, Pc_mais_1};  // Bit_Extender bit_extender_4
  Multiplexer #(.width(32)) multiplexer_4 (.in0(rs2_out), .in1(Imm), .out(multiplexer_4_out), .sel(IMM_ULA));
  ULA ula_1 (.Rs1(rs1_out), .Rs2(multiplexer_4_out), .op_ula(OP_ULA), .D(Ula_result));
  RAM #(.addrWidth(24), .dataWidth(32)) ram_1 (
    .addr(bit_extender_5_out), .we(W_MEM), .oe(1'b1), .clk(clk), .din(rs2_out), .dout(mem_out));
  Bit_Extender #(.in_width(32), .out_width(24)) bit_extender_5 (.in(Ula_result), .out(bit_extender_5_out));

  // Notes on the sheet:
  //   contents of rom_1 (hex, n*v repeats v):
  //   a1002 1e1003 234 2245 f1006 23066 34007 51009 508a 5078 7200 600b a1002 a1003 51004 1007 28320 11077
  //   28420 11077 29420 11077 29320 11077 2a240 11077 2a320 11077 2b420 11077 2b240 11077 a1002 c1003 c324
  //   d325 e000
endmodule

module banco_reg (
  input  Reset,
  input  CLK,
  input  [31:0] D,
  input  [3:0] RS1_in,
  input  WE,
  input  [3:0] rd,
  input  [3:0] RS2_in,
  output [31:0] RS1_out,
  output [31:0] RS2_out
);

  wire demultiplexer_1_out1, demultiplexer_1_out2, demultiplexer_1_out3, demultiplexer_1_out4,
       demultiplexer_1_out5, demultiplexer_1_out6, demultiplexer_1_out7, demultiplexer_1_out8,
       demultiplexer_1_out9, demultiplexer_1_out10, demultiplexer_1_out11, demultiplexer_1_out12,
       demultiplexer_1_out13, demultiplexer_1_out14, demultiplexer_1_out15;
  wire [31:0] X1, X2, X3, X4, X5, X6, X7, X8, X9, X10, X11, X12, X13, X14, X15;

  Demultiplexer #(.select(4)) demultiplexer_1 (
    .out1(demultiplexer_1_out1), .out2(demultiplexer_1_out2), .out3(demultiplexer_1_out3),
    .out4(demultiplexer_1_out4), .out5(demultiplexer_1_out5), .out6(demultiplexer_1_out6),
    .out7(demultiplexer_1_out7), .out8(demultiplexer_1_out8), .out9(demultiplexer_1_out9),
    .out10(demultiplexer_1_out10), .out11(demultiplexer_1_out11), .out12(demultiplexer_1_out12),
    .out13(demultiplexer_1_out13), .out14(demultiplexer_1_out14), .out15(demultiplexer_1_out15), .in(WE),
    .sel(rd));  // open: out0
  Register #(.width(32)) SP (.D(D), .en(demultiplexer_1_out1), .clk(CLK), .Q(X1), .clr(Reset));
  Register #(.width(32)) T0 (.D(D), .en(demultiplexer_1_out2), .clk(CLK), .Q(X2), .clr(Reset));
  Register #(.width(32)) T1 (.D(D), .en(demultiplexer_1_out3), .clk(CLK), .Q(X3), .clr(Reset));
  Register #(.width(32)) T2 (.D(D), .en(demultiplexer_1_out4), .clk(CLK), .Q(X4), .clr(Reset));
  Register #(.width(32)) T3 (.D(D), .en(demultiplexer_1_out5), .clk(CLK), .Q(X5), .clr(Reset));
  Register #(.width(32)) S0 (.D(D), .en(demultiplexer_1_out6), .clk(CLK), .Q(X6), .clr(Reset));
  Register #(.width(32)) S1 (.D(D), .en(demultiplexer_1_out7), .clk(CLK), .Q(X7), .clr(Reset));
  Register #(.width(32)) S2 (.D(D), .en(demultiplexer_1_out8), .clk(CLK), .Q(X8), .clr(Reset));
  Register #(.width(32)) S3 (.D(D), .en(demultiplexer_1_out9), .clk(CLK), .Q(X9), .clr(Reset));
  Register #(.width(32)) S4 (.D(D), .en(demultiplexer_1_out10), .clk(CLK), .Q(X10), .clr(Reset));
  Register #(.width(32)) S5 (.D(D), .en(demultiplexer_1_out11), .clk(CLK), .Q(X11), .clr(Reset));
  Register #(.width(32)) A0 (.D(D), .en(demultiplexer_1_out12), .clk(CLK), .Q(X12), .clr(Reset));
  Register #(.width(32)) A1 (.D(D), .en(demultiplexer_1_out13), .clk(CLK), .Q(X13), .clr(Reset));
  Register #(.width(32)) A2 (.D(D), .en(demultiplexer_1_out14), .clk(CLK), .Q(X14), .clr(Reset));
  Register #(.width(32)) RA (.D(D), .en(demultiplexer_1_out15), .clk(CLK), .Q(X15), .clr(Reset));
  Multiplexer #(.select(4), .width(32)) multiplexer_1 (
    .in0({32{1'b0}}), .in1(X1), .in2(X2), .in3(X3), .in4(X4), .in5(X5), .in6(X6), .in7(X7), .in8(X8),
    .in9(X9), .in10(X10), .in11(X11), .in12(X12), .in13(X13), .in14(X14), .in15(X15), .out(RS1_out),
    .sel(RS1_in));
  Multiplexer #(.select(4), .width(32)) multiplexer_2 (
    .in0({32{1'b0}}), .in1(X1), .in2(X2), .in3(X3), .in4(X4), .in5(X5), .in6(X6), .in7(X7), .in8(X8),
    .in9(X9), .in10(X10), .in11(X11), .in12(X12), .in13(X13), .in14(X14), .in15(X15), .out(RS2_out),
    .sel(RS2_in));

  // Other names for the same wires on the sheet: CLK_t = CLK; D_t[31:0] = D; R_t = Reset

  // Notes on the sheet:
  //   X0
endmodule

module ULA (
  input  [31:0] Rs1,
  input  [31:0] Rs2,
  input  [2:0] op_ula,
  output [31:0] D
);

  wire [4:0] bit_extender_1_out;
  wire [31:0] adder_1_out, and_1_out, or_1_out, shifter_1_out, subtractor_1_out;

  Bit_Extender #(.in_width(32), .out_width(5), .\type ("zero")) bit_extender_1 (.in(Rs2), .out(bit_extender_1_out));
  assign and_1_out = Rs1 & Rs2;  // AND_Gate and_1, 32 bits wide
  assign or_1_out = Rs1 | Rs2;  // OR_Gate or_1, 32 bits wide
  Adder #(.width(32)) adder_1 (.a(Rs1), .b(Rs2), .out(adder_1_out));  // open: cin, cout
  Subtractor #(.width(32)) subtractor_1 (.a(Rs1), .b(Rs2), .out(subtractor_1_out));  // open: bin, bout
  Shifter #(.width(32)) shifter_1 (.in(Rs1), .\dist (bit_extender_1_out), .out(shifter_1_out));
  Multiplexer #(.select(3), .width(32)) multiplexer_1 (
    .in0(adder_1_out), .in1(subtractor_1_out), .in2(shifter_1_out), .in3(and_1_out), .in4(or_1_out), .out(D),
    .sel(op_ula));  // open: in5, in6, in7
endmodule

module branches (
  input  [31:0] rs1,
  input  [31:0] rs2,
  input  B,
  input  [1:0] B_in,
  output B_out
);

  wire comparator_1_eq, comparator_1_gt, comparator_1_lt, not_1_out, or_1_out;

  Comparator #(.width(32)) comparator_1 (
    .a(rs1), .b(rs2), .gt(comparator_1_gt), .eq(comparator_1_eq), .lt(comparator_1_lt));
  or or_1 (or_1_out, comparator_1_gt, comparator_1_eq);
  not not_1 (not_1_out, comparator_1_eq);
  Multiplexer #(.enable("true"), .select(2)) multiplexer_1 (
    .in0(comparator_1_eq), .in1(comparator_1_lt), .in2(not_1_out), .in3(or_1_out), .out(B_out), .sel(B_in),
    .en(B));
endmodule

module unit_control (
  input  [3:0] OpCode,
  output IMM_ULA,
  output W_RG,
  output W_MEM,
  output [1:0] PC_M,
  output B,
  output [1:0] D_RG,
  output [1:0] B_IN,
  output [2:0] OP_ULA,
  output W_PC,
  output RESET
);

  wire and_1_out, and_2_out, and_4_out, and_5_out, and_6_out, and_7_out, and_10_out, and_11_out, and_12_out,
       and_13_out, and_15_out, and_23_out, or_1_out, or_2_out, or_3_out, or_5_out, S1_N, S2_N, S3_N, S4_N;

  not not_1 (S1_N, OpCode[0]);
  not not_2 (S2_N, OpCode[1]);
  not not_3 (S3_N, OpCode[2]);
  not not_4 (S4_N, OpCode[3]);
  and and_1 (and_1_out, S3_N, OpCode[3]);
  and and_2 (and_2_out, OpCode[0], OpCode[1], OpCode[2], S4_N);
  and and_3 (B, S3_N, OpCode[3]);
  and and_4 (and_4_out, S2_N, S3_N);
  and and_5 (and_5_out, OpCode[1], S3_N);
  and and_6 (and_6_out, S2_N, OpCode[2]);
  and and_7 (and_7_out, OpCode[1], OpCode[2]);
  or or_1 (or_1_out, and_1_out, and_2_out);
  not not_5 (W_RG, or_1_out);
  and and_8 (D_RG[0], S1_N, OpCode[1], OpCode[2], S4_N);
  and and_9 (D_RG[1], S2_N, OpCode[2], S4_N);
  and and_10 (and_10_out, OpCode[1], S3_N, S4_N);
  or or_2 (or_2_out, and_10_out, and_11_out);
  and and_11 (and_11_out, S2_N, OpCode[2], OpCode[3]);
  and and_12 (and_12_out, OpCode[0], OpCode[1], S3_N, S4_N);
  and and_13 (and_13_out, S1_N, S2_N, OpCode[2], OpCode[3]);
  and and_14 (OP_ULA[2], OpCode[0], S2_N, OpCode[2], OpCode[3]);
  or or_3 (or_3_out, and_4_out, and_5_out, and_6_out);
  and and_15 (and_15_out, or_3_out, OpCode[0]);
  and and_16 (OP_ULA[0], S1_N, or_2_out);
  or or_4 (OP_ULA[1], and_12_out, and_13_out);
  or or_5 (or_5_out, and_15_out, and_7_out);
  and and_17 (IMM_ULA, or_5_out, S4_N);
  and and_18 (W_MEM, OpCode[0], OpCode[1], OpCode[2], S4_N);
  and and_19 (PC_M[0], S4_N, OpCode[2], S2_N, S1_N);
  and and_20 (PC_M[1], S4_N, OpCode[2], S2_N, OpCode[0]);
  and and_21 (B_IN[0], OpCode[3], S3_N, OpCode[1]);
  and and_22 (B_IN[1], OpCode[3], S3_N, OpCode[0]);
  and and_23 (and_23_out, S1_N, OpCode[1], OpCode[2], OpCode[3]);
  and and_24 (RESET, OpCode[0], OpCode[1], OpCode[2], OpCode[3]);
  not not_6 (W_PC, and_23_out);

  // Other names for the same wires on the sheet: S1 = OpCode[0]; S2 = OpCode[1]; S3 = OpCode[2]; S4 = OpCode[3]
endmodule
